# Fritzing sketch smart_home_devre (saved by Fritzing 0.9.3b)
breadboards: 1

parts:
  Eleman1 = Arduino Uno (Rev3)
  Eleman2 = Bluetooth HC-06
  R3 = Resistor [tolerance=±5% resistance=10k package=THT]
  R4 = Resistor [tolerance=±5% resistance=10k package=THT]
  R5 = Photocell (LDR) [package=THT]
  LED1 = LED - 5mm [color="Red (633nm)" package="5 mm [THT]"]
  R7 = Resistor [tolerance=±5% resistance=330 package=THT]
  LED3 = LED - 5mm [color="Red (633nm)" package="5 mm [THT]"]
  LED4 = LED - 5mm [color="Red (633nm)" package="5 mm [THT]"]
  R8 = Resistor [tolerance=±5% resistance=330 package=THT]
  J2 = Basic Servo
  J3 = Piezo Speaker
  LED5 = LED - 5mm [color="Red (633nm)" package="5 mm [THT]"]
  LED6 = LED - 5mm [color="Red (633nm)" package="5 mm [THT]"]
  R9 = Resistor [tolerance=±5% resistance=330 package=THT]
  R10 = Resistor [tolerance=±5% resistance=330 package=THT]
  U1 = GAS_SENSOR [package=mq-3]  # not connected

nets:
  N1: Eleman1.A0, R3.Pin_1
  N2: Eleman1.A1, R4.Pin_0, R5.pin_0
  N3: Eleman1.D8, R10.Pin_0
  N4: Eleman1.D9_PWM, J2.pulse
  N5: Eleman1.D10_PWM/SS, R9.Pin_0
  N6: Eleman1.D11_PWM/MOSI, J3.pin2
  N7: Eleman1.D13/SCK, R8.Pin_0
  N8: Eleman1.D0/RX, Eleman2.TXD
  N9: Eleman1.D1/TX, Eleman2.RXD
  N10: Eleman1.D3_PWM, R7.Pin_0
  VCC: Eleman1.5V, Eleman2.VCC, R5.pin_1, J2.vcc
  GND: Eleman1.GND, Eleman2.GND, R3.Pin_0, R4.Pin_1, LED1.cathode, LED3.cathode, LED4.cathode, J2.gnd, J3.pin1, LED5.cathode, LED6.cathode

notes:
  LDR (Işık Şiddeti Ölçer)
  LED (Dış Aydınlatma)
  LED (Salon Lamba)
  Servo Motor (Kapı Açma/Kapama)
  Buzzer (Sesli Bildirim Aracı)
  Bluetooth Sensörü
  FAN (Klima)
  LED [Yatak Odası Lamba]
  LED [Mutfak Lamba]
  MQ2 Gaz Sensörü
